# Fritzing sketch wiring_sensors (saved by Fritzing 0.9.3b)
breadboards: 1

parts:
  Bauteil1 = Logic Level Converter
  Raspberry_Pi1 = Raspberry Pi B+

nets:
  N1: Bauteil1.GND, Raspberry_Pi1.GPIO21, Raspberry_Pi1.GPIO20
  N2: Bauteil1.LV, Bauteil1.HV, Raspberry_Pi1.5V
